// Logisim project practica2IC.circ as structural Verilog: 1 circuit, main circuit main
module main (
  input  a,
  input  b,
  input  c,
  input  d,
  output Z,
  output Z2,
  output Z3
);

  wire and_1_out, and_2_out, and_3_out, and_4_out, and_5_out, and_6_out, and_7_out, and_8_out, and_9_out,
       nor_1_out, nor_2_out, nor_3_out, nor_4_out, nor_5_out, nor_6_out, not_1_out, not_2_out, not_3_out,
       not_4_out, not_5_out, not_6_out, not_7_out, not_8_out, not_9_out, not_10_out, not_11_out, not_12_out,
       not_13_out, not_14_out, not_15_out, not_16_out, not_17_out, not_18_out, not_19_out, not_20_out,
       or_1_out, or_2_out;

  and and_1 (and_1_out, a, b);
  and and_2 (and_2_out, c, d);
  and and_3 (and_3_out, d, a);
  and and_4 (and_4_out, b, c);
  not not_1 (not_1_out, a);
  not not_2 (not_2_out, b);
  not not_3 (not_3_out, c);
  not not_4 (not_4_out, d);
  not not_5 (not_5_out, a);
  not not_6 (not_6_out, b);
  not not_7 (not_7_out, c);
  not not_8 (not_8_out, a);
  not not_9 (not_9_out, b);
  not not_10 (not_10_out, d);
  not not_11 (not_11_out, a);
  not not_12 (not_12_out, c);
  not not_13 (not_13_out, d);
  not not_14 (not_14_out, b);
  not not_15 (not_15_out, c);
  not not_16 (not_16_out, d);
  not not_17 (not_17_out, a);
  not not_18 (not_18_out, b);
  not not_19 (not_19_out, c);
  not not_20 (not_20_out, d);
  or or_1 (or_1_out, and_1_out, and_2_out);
  or or_2 (or_2_out, and_3_out, and_4_out);
  and and_5 (and_5_out, not_1_out, b, c, d);
  and and_6 (and_6_out, a, not_3_out, b, d);
  and and_7 (and_7_out, a, b, c, not_4_out);
  and and_8 (and_8_out, a, b, c, d);
  and and_9 (and_9_out, a, c, not_2_out, d);
  nor nor_1 (nor_1_out, d, not_5_out, not_6_out, not_7_out);
  nor nor_2 (nor_2_out, not_8_out, not_9_out, not_10_out, c);
  nor nor_3 (nor_3_out, not_11_out, not_12_out, not_13_out, b);
  nor nor_4 (nor_4_out, not_14_out, not_15_out, not_16_out, a);
  nor nor_5 (nor_5_out, not_17_out, not_18_out, not_19_out, not_20_out);
  and and_10 (Z, or_1_out, or_2_out);
  or or_3 (Z2, and_5_out, and_9_out, and_6_out, and_7_out, and_8_out);
  nor nor_6 (nor_6_out, nor_1_out, nor_2_out, nor_3_out, nor_4_out, nor_5_out);
  not not_21 (Z3, nor_6_out);
endmodule
