// Logisim project practica3IC.circ as structural Verilog: 5 circuits, main circuit main
module main (
  input  x3,
  input  x2,
  input  x1,
  input  x0
);

  wire a, b, c, d, e, f, g, s;

  circuito1 circuito1_1 (.x3(x3), .x2(x2), .x1(x1), .x0(x0), .s(s), .a(a), .b(b), .c(c), .d(d), .e(e), .f(f), .g(g));
  _7_Segment_Display u_7_segment_display_1 (.g(g), .f(f), .a(a), .b(b), .e(e), .d(d), .c(c));  // open: dp
  _7_Segment_Display u_7_segment_display_2 (.g(s));  // open: f, a, b, e, d, c, dp
endmodule

module circuito1 (
  input  x3,
  input  x2,
  input  x1,
  input  x0,
  output s,
  output a,
  output b,
  output c,
  output d,
  output e,
  output f,
  output g
);

  wire and_1_out, and_2_out, and_3_out, and_4_out, and_5_out, and_6_out, and_7_out, and_8_out, and_9_out,
       and_10_out, and_11_out, and_12_out, and_13_out, and_14_out, and_15_out, and_16_out, and_17_out,
       and_18_out, and_19_out, and_20_out, and_21_out, and_22_out, and_23_out, and_24_out, and_25_out,
       and_26_out, not_1_out, not_2_out, not_3_out, not_4_out, not_5_out, not_6_out, not_7_out, not_8_out,
       not_9_out, not_10_out, not_11_out, not_12_out, not_13_out, not_14_out, not_15_out, not_16_out,
       not_17_out, not_18_out, not_19_out, not_20_out, not_21_out, not_22_out, not_23_out, not_24_out,
       not_25_out, not_26_out, not_27_out, not_28_out, not_29_out, not_30_out, not_31_out, not_32_out,
       not_33_out, not_34_out, not_35_out;

  not not_1 (not_1_out, x2);
  and and_1 (and_1_out, not_1_out, not_2_out);
  not not_2 (not_2_out, x0);
  not not_3 (not_3_out, x3);
  and and_2 (and_2_out, not_3_out, x1);
  and and_3 (and_3_out, x1, not_4_out);
  not not_4 (not_4_out, x0);
  and and_4 (and_4_out, x2, not_5_out, x0);
  not not_5 (not_5_out, x1);
  and and_5 (and_5_out, x3, not_6_out);
  not not_6 (not_6_out, x2);
  not not_7 (not_7_out, x3);
  and and_6 (and_6_out, not_7_out, not_8_out);
  not not_8 (not_8_out, x2);
  not not_9 (not_9_out, x2);
  and and_7 (and_7_out, not_9_out, not_10_out);
  not not_10 (not_10_out, x1);
  not not_11 (not_11_out, x1);
  and and_8 (and_8_out, not_11_out, not_12_out);
  not not_12 (not_12_out, x0);
  not not_13 (not_13_out, x3);
  and and_9 (and_9_out, not_13_out, x1, x0);
  and and_10 (and_10_out, x3, x2);
  not not_14 (not_14_out, x1);
  not not_15 (not_15_out, x3);
  and and_11 (and_11_out, not_15_out, x2);
  and and_12 (and_12_out, x3, not_16_out);
  not not_16 (not_16_out, x2);
  not not_17 (not_17_out, x2);
  and and_13 (and_13_out, not_17_out, not_18_out);
  not not_18 (not_18_out, x0);
  not not_19 (not_19_out, x2);
  and and_14 (and_14_out, not_19_out, x1);
  and and_15 (and_15_out, x1, not_20_out);
  not not_20 (not_20_out, x0);
  not not_21 (not_21_out, x1);
  and and_16 (and_16_out, x2, not_21_out, x0);
  not not_22 (not_22_out, x2);
  and and_17 (and_17_out, not_22_out, not_23_out);
  not not_23 (not_23_out, x0);
  and and_18 (and_18_out, x1, not_24_out);
  not not_24 (not_24_out, x0);
  not not_25 (not_25_out, x1);
  and and_19 (and_19_out, not_25_out, not_26_out);
  not not_26 (not_26_out, x0);
  not not_27 (not_27_out, x3);
  and and_20 (and_20_out, not_27_out, x2, not_28_out);
  not not_28 (not_28_out, x1);
  not not_29 (not_29_out, x3);
  and and_21 (and_21_out, not_29_out, x2, not_30_out);
  not not_30 (not_30_out, x0);
  and and_22 (and_22_out, x3, not_31_out, x1);
  not not_31 (not_31_out, x2);
  not not_32 (not_32_out, x2);
  and and_23 (and_23_out, not_32_out, x1);
  and and_24 (and_24_out, x2, not_33_out);
  not not_33 (not_33_out, x1);
  and and_25 (and_25_out, x2, not_34_out);
  not not_34 (not_34_out, x0);
  and and_26 (and_26_out, x3, not_35_out);
  not not_35 (not_35_out, x0);
  or or_1 (a, and_1_out, and_2_out, and_3_out, and_4_out, and_5_out);
  or or_2 (b, and_6_out, and_7_out, and_8_out, and_9_out, and_10_out);
  or or_3 (c, not_14_out, x0, and_11_out, and_12_out);
  or or_4 (d, and_13_out, and_14_out, and_15_out, and_16_out);
  or or_5 (e, and_17_out, and_18_out);
  or or_6 (f, and_19_out, and_20_out, and_21_out, and_22_out);
  or or_7 (g, and_23_out, and_24_out, and_25_out, and_26_out);

  assign s = x3;
endmodule

module RCA4 (
  input  x3,
  input  in_2,
  input  x2,
  input  x1,
  input  x0,
  input  Y3,
  input  Y2,
  input  Y1,
  input  Y0
);

  wire a0, a2, a3, b0, b2, b3, c0, c2, c3, d0, d2, d3, e0, e2, e3, f0, f2, f3, g0, g2, g3, s0, s2, s3, Z0,
       Z1, Z2, Z3;

  Sumador sumador_1 (
    .Y3(Y3), .X3(x3), .Y2(Y2), .X2(x2), .Y1(Y1), .X1(x1), .in_9(in_2), .Y0(Y0), .X0(x0), .Z3(Z3), .Z2(Z2),
    .Z1(Z1), .Z0(Z0));
  circuito1 circuito1_1 (
    .x3(x3), .x2(x2), .x1(x1), .x0(x0), .s(s0), .a(a0), .b(b0), .c(c0), .d(d0), .e(e0), .f(f0), .g(g0));
  circuito1 circuito1_2 (
    .x3(Y3), .x2(Y2), .x1(Y1), .x0(Y0), .s(s2), .a(a2), .b(b2), .c(c2), .d(d2), .e(e2), .f(f2), .g(g2));
  circuito1 circuito1_3 (
    .x3(Z3), .x2(Z2), .x1(Z1), .x0(Z0), .s(s3), .a(a3), .b(b3), .c(c3), .d(d3), .e(e3), .f(f3), .g(g3));
  _7_Segment_Display u_7_segment_display_1 (.g(s0));  // open: f, a, b, e, d, c, dp
  _7_Segment_Display u_7_segment_display_2 (.g(s2));  // open: f, a, b, e, d, c, dp
  _7_Segment_Display u_7_segment_display_3 (.g(g0), .f(f0), .a(a0), .b(b0), .e(e0), .d(d0), .c(c0));  // open: dp
  _7_Segment_Display u_7_segment_display_4 (.g(g2), .f(f2), .a(a2), .b(b2), .e(e2), .d(d2), .c(c2));  // open: dp
  _7_Segment_Display u_7_segment_display_5 (.g(g3), .f(f3), .a(a3), .b(b3), .e(e3), .d(d3), .c(c3));  // open: dp
  _7_Segment_Display u_7_segment_display_6 (.g(s3));  // open: f, a, b, e, d, c, dp
endmodule

module FA (
  input  A,
  input  B,
  input  Ci,
  output S,
  output Co
);

  wire and_1_out, and_2_out, xor_1_out;

  xor xor_1 (xor_1_out, A, B);
  xor xor_2 (S, xor_1_out, Ci);
  and and_1 (and_1_out, xor_1_out, Ci);
  and and_2 (and_2_out, A, B);
  or or_1 (Co, and_1_out, and_2_out);
endmodule

module Sumador (
  input  X3,
  input  X2,
  input  X1,
  input  X0,
  input  Y3,
  input  Y2,
  input  Y1,
  input  Y0,
  input  in_9,
  output Z3,
  output Z2,
  output Z1,
  output Z0
);

  wire fa_2_co, fa_3_co, fa_4_co;

  FA fa_1 (.A(X3), .B(Y3), .Ci(fa_2_co), .S(Z3));  // open: Co
  FA fa_2 (.A(X2), .B(Y2), .Ci(fa_3_co), .S(Z2), .Co(fa_2_co));
  FA fa_3 (.A(X1), .B(Y1), .Ci(fa_4_co), .S(Z1), .Co(fa_3_co));
  FA fa_4 (.A(X0), .B(Y0), .Ci(in_9), .S(Z0), .Co(fa_4_co));
endmodule
