// Logisim project practica5IC.circ as structural Verilog: 5 circuits, main circuit main
module main (
);

  AddGen addgen_1 ();  // open: reset, en, q2, q1, q0, fin
  ALU alu_1 ();  // open: A, B, N, Z, V, C, in_3, in_4, out_5
  ROM rom_1 ();  // open: addr, data, sel
endmodule

module AddGen (
  input  reset,
  input  en,
  output q2,
  output q1,
  output q0,
  output fin
);

  wire and_2_out, and_3_out, and_4_out, clk_out, not_1_out, not_2_out, not_3_out, not_4_out, or_1_out,
       or_2_out, or_3_out, or_4_out;

  Clock clk (.out(clk_out));
  and and_1 (fin, q0, q1, q2);
  or or_1 (or_1_out, en, q2);
  or or_2 (or_2_out, q2, q1);
  or or_3 (or_3_out, q2, q0);
  not not_1 (not_1_out, en);
  not not_2 (not_2_out, q2);
  not not_3 (not_3_out, q1);
  not not_4 (not_4_out, q0);
  and and_2 (and_2_out, en, q0);
  and and_3 (and_3_out, en, q0);
  and and_4 (and_4_out, or_1_out, or_2_out, or_3_out, or_4_out);
  or or_4 (or_4_out, not_1_out, not_2_out, not_3_out, not_4_out);
  D_Flip_Flop d_ff_1 (.clk(clk_out), .D(and_4_out), .Q(q2), .reset(reset));  // open: Qn, preset, en
  J_K_Flip_Flop j_k_ff_1 (.J(and_2_out), .clk(clk_out), .K(and_3_out), .Q(q1), .reset(reset));  // open: Qn, preset, en
  T_Flip_Flop t_ff_1 (.clk(clk_out), .T(en), .Q(q0), .reset(reset));  // open: Qn, preset, en
endmodule

module MUX_4_1 (
  input  X0,
  input  X1,
  input  X2,
  input  X3,
  input  s1,
  input  s0,
  output Z
);

  wire and_1_out, and_2_out, and_3_out, and_4_out, not_1_out, not_2_out;

  not not_1 (not_1_out, s1);
  not not_2 (not_2_out, s0);
  and and_1 (and_1_out, X0, not_1_out, not_2_out);
  and and_2 (and_2_out, X1, not_1_out, s0);
  and and_3 (and_3_out, X2, s1, not_2_out);
  and and_4 (and_4_out, X3, s1, s0);
  or or_1 (Z, and_1_out, and_2_out, and_3_out, and_4_out);
endmodule

module MUX_4_1x16 (
  input  [15:0] x0,
  input  [15:0] x1,
  input  [15:0] x2,
  input  [15:0] x3,
  input  s1,
  input  s0,
  output [15:0] z
);

  MUX_4_1 mux_4_1_1 (.X0(x0[0]), .X1(x1[0]), .X2(x2[1]), .X3(x3[0]), .s1(s1), .s0(s0), .Z(z[0]));
  MUX_4_1 mux_4_1_2 (.X0(x0[1]), .X1(x1[1]), .X2(x2[1]), .X3(x3[1]), .s1(s1), .s0(s0), .Z(z[1]));
  MUX_4_1 mux_4_1_3 (.X0(x0[2]), .X1(x1[2]), .X2(x2[2]), .X3(x3[3]), .s1(s1), .s0(s0), .Z(z[2]));
  MUX_4_1 mux_4_1_4 (.X0(x0[3]), .X1(x1[3]), .X2(x2[3]), .X3(x3[2]), .s1(s1), .s0(s0), .Z(z[3]));
  MUX_4_1 mux_4_1_5 (.X0(x0[4]), .X1(x1[4]), .X2(x2[4]), .X3(x3[4]), .s1(s1), .s0(s0), .Z(z[4]));
  MUX_4_1 mux_4_1_6 (.X0(x0[5]), .X1(x1[5]), .X2(x2[5]), .X3(x3[5]), .s1(s1), .s0(s0), .Z(z[5]));
  MUX_4_1 mux_4_1_7 (.X0(x0[6]), .X1(x1[6]), .X2(x2[6]), .X3(x3[6]), .s1(s1), .s0(s0), .Z(z[6]));
  MUX_4_1 mux_4_1_8 (.X0(x0[7]), .X1(x1[7]), .X2(x2[7]), .X3(x3[7]), .s1(s1), .s0(s0), .Z(z[7]));
  MUX_4_1 mux_4_1_9 (.X0(x0[8]), .X1(x1[8]), .X2(x2[8]), .X3(x3[8]), .s1(s1), .s0(s0), .Z(z[8]));
  MUX_4_1 mux_4_1_10 (.X0(x0[9]), .X1(x1[9]), .X2(x2[9]), .X3(x3[9]), .s1(s1), .s0(s0), .Z(z[9]));
  MUX_4_1 mux_4_1_11 (.X0(x0[10]), .X1(x1[10]), .X2(x2[10]), .X3(x3[10]), .s1(s1), .s0(s0), .Z(z[10]));
  MUX_4_1 mux_4_1_12 (.X0(x0[11]), .X1(x1[11]), .X2(x2[11]), .X3(x3[11]), .s1(s1), .s0(s0), .Z(z[11]));
  MUX_4_1 mux_4_1_13 (.X0(x0[12]), .X1(x1[12]), .X2(x2[12]), .X3(x3[12]), .s1(s1), .s0(s0), .Z(z[12]));
  MUX_4_1 mux_4_1_14 (.X0(x0[13]), .X1(x1[13]), .X2(x2[13]), .X3(x3[13]), .s1(s1), .s0(s0), .Z(z[13]));
  MUX_4_1 mux_4_1_15 (.X0(x0[14]), .X1(x1[14]), .X2(x2[14]), .X3(x3[14]), .s1(s1), .s0(s0), .Z(z[14]));
  MUX_4_1 mux_4_1_16 (.X0(x0[15]), .X1(x1[15]), .X2(x2[15]), .X3(x3[15]), .s1(s1), .s0(s0), .Z(z[15]));

  assign x2[0] = x2[1];
endmodule

module ALU (
  input  [15:0] A,
  input  [15:0] B,
  input  in_3,
  input  in_4,
  output [15:0] out_5,
  output N,
  output Z,
  output V,
  output C
);

  wire and_1_out, and_2_out, b15_prime, Cout0, Cout1, not_2_out, not_3_out, not_4_out, not_5_out;
  wire [15:0] adder_1_out, adder_2_out, not_1_out, xor_1_out;

  assign not_1_out = ~B;  // NOT_Gate not_1, 16 bits wide
  Adder #(.width(16)) adder_1 (.a(A), .b(not_1_out), .out(adder_1_out), .cin(1'b1), .cout(Cout1));
  or or_1 (C, Cout0, Cout1);
  Adder #(.width(16)) adder_2 (.a(A), .b(B), .out(adder_2_out), .cin(1'b0), .cout(Cout0));
  assign xor_1_out = A ^ B;  // XOR_Gate xor_1, 16 bits wide
  MUX_4_1 mux_4_1_1 (.X0(A[15]), .X3(not_2_out), .s1(in_3), .s0(in_3), .Z(b15_prime));  // open: X1, X2
  not not_2 (not_2_out, A[15]);
  MUX_4_1x16 mux_4_1x16_1 (
    .x0(adder_2_out), .x1(B), .x2(xor_1_out), .x3(adder_1_out), .s1(in_3), .s0(in_4), .z({N, out_5[14:0]}));
  not not_3 (not_3_out, B[15]);
  not not_4 (not_4_out, b15_prime);
  not not_5 (not_5_out, N);
  nor nor_1 (Z, out_5[0], out_5[1], out_5[2], out_5[3], out_5[4], out_5[5], out_5[6], out_5[7], out_5[8], out_5[9], out_5[10], out_5[11], out_5[12], out_5[13], out_5[14], N);
  and and_1 (and_1_out, not_3_out, not_4_out, N);
  and and_2 (and_2_out, B[15], b15_prime, not_5_out);
  or or_2 (V, and_1_out, and_2_out);

  assign out_5[15] = N;

  // Other names for the same wires on the sheet: b15 = A[15]; a15 = B[15]; s15 = N; T0 = in_4; T1 = in_3
endmodule
