// Logisim project 723367-3.circ as structural Verilog: 5 circuits, main circuit main
module main (
);

  wire a_t, alu_1_z, and_1_out, b, button_2_out, button_3_out, clk, clock_1_out, FZ, fz_t, ir, nL_E,
       not_1_out, pc_t, reset, tty_out_1_clr, tty_out_1_out;
  wire [1:0] alu, CO, mux;
  wire [2:0] estado, rom_1_data;
  wire [6:0] A, adder_1_out, D, D6_0, F, PC;
  wire [9:0] adder_2_out, register_1_q;
  wire [15:0] A_q, B_q, ram_1_data;
  wire [15:7] alu_1_out_5;

  Register #(.width(3)) u_estado (.D(rom_1_data), .Q(estado), .clk(clk), .clr(reset));  // open: en
  Register #(.width(7)) u_PC (.D(adder_1_out), .en(pc_t), .Q(PC), .clk(clk), .clr(reset));
  Register #(.width(16)) u_IR (.D(ram_1_data), .en(ir), .Q({CO, F, D}), .clk(clk));  // open: clr
  Multiplexer #(.select(2), .width(7), .enable("false")) multiplexer_1 (
    .in0(PC), .in2(F), .in3(D), .out(A), .sel(mux));  // open: in1
  ROM #(.addrWidth(6), .dataWidth(3)) rom_1 (.addr({estado, CO, FZ}), .data(rom_1_data));  // open: sel
  ROM #(.addrWidth(3), .dataWidth(10)) rom_2 (
    .addr(estado), .data({mux, alu, nL_E, pc_t, ir, a_t, b, fz_t}));  // open: sel
  Adder #(.width(7)) adder_1 (.a(7'b0000001), .b(A), .out(adder_1_out));  // open: cin, cout
  Register #(.width(16)) u_A (.D(ram_1_data), .en(a_t), .Q(A_q), .clk(clk));  // open: clr
  Register #(.width(1)) u_FZ (.D(alu_1_z), .en(fz_t), .Q(FZ), .clk(clk));  // open: clr
  ALU alu_1 (
    .A(A_q), .B(B_q), .Z(alu_1_z), .in_3(alu[1]), .in_4(alu[0]), .out_5({alu_1_out_5, D6_0}));  // open: N, V, C
  // Probe on PC
  // Probe on CO
  Register #(.width(16)) u_B (.D(ram_1_data), .en(b), .Q(B_q), .clk(clk));  // open: clr
  Button button_1 (.out(reset));
  Button button_2 (.out(button_2_out));
  Clock clock_1 (.out(clock_1_out));
  // Probe on F
  // Probe on D
  RAM #(.addrWidth(7), .dataWidth(16), .bus("separate")) ram_1 (
    .addr(A), .din({alu_1_out_5, D6_0}), .data(ram_1_data), .str(nL_E), .sel(1'b1), .clk(clk), .ld(not_1_out));  // open: clr
  not not_1 (not_1_out, nL_E);
  Button button_3 (.out(button_3_out));
  and and_1 (and_1_out, button_2_out, clock_1_out);
  // Probe on estado
  TTY tty_1 (.data(D6_0), .clk(clk), .we(tty_out_1_out), .clr(tty_out_1_clr));
  tty_out tty_out_1 (.A(A), .E(nL_E), .out(tty_out_1_out), .clr(tty_out_1_clr), .D(D6_0), .clk(clk));
  or or_1 (clk, button_3_out, and_1_out);
  Register #(.width(10)) register_1 (.D(adder_2_out), .Q(register_1_q), .clk(clk), .clr(reset));  // open: en
  Adder #(.width(10)) adder_2 (.a(10'h1), .b(register_1_q), .out(adder_2_out));  // open: cin, cout
  // Probe on adder_2_out

  // Notes on the sheet:
  //   Unidad de Control (cableada 12 estados)
  //   Unidad de Proceso (ruta de datos)
  //   contents of rom_1 (hex, n*v repeats v):
  //   8*1 4*2 5 5 0 6 3 3 4 4 3 3 4 4 24*0 8*1
  //   contents of rom_2 (hex, n*v repeats v):
  //   18 202 304 321 41 3a1 318
  //   Control de simulación
  //   0 ADD
  //   1 CMP
  //   2 MOV
  //   3 BEQ
endmodule

module tty_out (
  input  clk,
  input  [6:0] A,
  input  E,
  input  [6:0] D,
  output out,
  output clr
);

  wire and_2_out, and_3_out;

  and and_1 (out, A[0], A[1], A[2], A[3], A[4], A[5], A[6], E);
  and and_2 (and_2_out, ~D[0], ~D[1], ~D[2], ~D[3], ~D[4], ~D[5], ~D[6]);  // AND_Gate
  and and_3 (and_3_out, out, and_2_out);
  D_Flip_Flop d_ff_1 (.clk(clk), .D(and_3_out), .Q(clr), .en(1'b1));  // open: Qn, preset, reset
endmodule

module MUX_4_1 (
  input  X0,
  input  X1,
  input  X2,
  input  X3,
  input  s1,
  input  s0,
  output Z
);

  wire and_1_out, and_2_out, and_3_out, and_4_out, not_1_out, not_2_out;

  not not_1 (not_1_out, s1);
  not not_2 (not_2_out, s0);
  and and_1 (and_1_out, X0, not_1_out, not_2_out);
  and and_2 (and_2_out, X1, not_1_out, s0);
  and and_3 (and_3_out, X2, s1, not_2_out);
  and and_4 (and_4_out, X3, s1, s0);
  or or_1 (Z, and_1_out, and_2_out, and_3_out, and_4_out);
endmodule

module MUX_4_1x16 (
  input  [15:0] x0,
  input  [15:0] x1,
  input  [15:0] x2,
  input  [15:0] x3,
  input  s1,
  input  s0,
  output [15:0] z
);

  MUX_4_1 mux_4_1_1 (.X0(x0[0]), .X1(x1[0]), .X2(x2[0]), .X3(x3[0]), .s1(s1), .s0(s0), .Z(z[0]));
  MUX_4_1 mux_4_1_2 (.X0(x0[1]), .X1(x1[1]), .X2(x2[1]), .X3(x3[1]), .s1(s1), .s0(s0), .Z(z[1]));
  MUX_4_1 mux_4_1_3 (.X0(x0[2]), .X1(x1[2]), .X2(x2[2]), .X3(x3[3]), .s1(s1), .s0(s0), .Z(z[2]));
  MUX_4_1 mux_4_1_4 (.X0(x0[3]), .X1(x1[3]), .X2(x2[3]), .X3(x3[2]), .s1(s1), .s0(s0), .Z(z[3]));
  MUX_4_1 mux_4_1_5 (.X0(x0[4]), .X1(x1[4]), .X2(x2[4]), .X3(x3[4]), .s1(s1), .s0(s0), .Z(z[4]));
  MUX_4_1 mux_4_1_6 (.X0(x0[5]), .X1(x1[5]), .X2(x2[5]), .X3(x3[5]), .s1(s1), .s0(s0), .Z(z[5]));
  MUX_4_1 mux_4_1_7 (.X0(x0[6]), .X1(x1[6]), .X2(x2[6]), .X3(x3[6]), .s1(s1), .s0(s0), .Z(z[6]));
  MUX_4_1 mux_4_1_8 (.X0(x0[7]), .X1(x1[7]), .X2(x2[7]), .X3(x3[7]), .s1(s1), .s0(s0), .Z(z[7]));
  MUX_4_1 mux_4_1_9 (.X0(x0[8]), .X1(x1[8]), .X2(x2[8]), .X3(x3[8]), .s1(s1), .s0(s0), .Z(z[8]));
  MUX_4_1 mux_4_1_10 (.X0(x0[9]), .X1(x1[9]), .X2(x2[9]), .X3(x3[9]), .s1(s1), .s0(s0), .Z(z[9]));
  MUX_4_1 mux_4_1_11 (.X0(x0[10]), .X1(x1[10]), .X2(x2[10]), .X3(x3[10]), .s1(s1), .s0(s0), .Z(z[10]));
  MUX_4_1 mux_4_1_12 (.X0(x0[11]), .X1(x1[11]), .X2(x2[11]), .X3(x3[11]), .s1(s1), .s0(s0), .Z(z[11]));
  MUX_4_1 mux_4_1_13 (.X0(x0[12]), .X1(x1[12]), .X2(x2[12]), .X3(x3[12]), .s1(s1), .s0(s0), .Z(z[12]));
  MUX_4_1 mux_4_1_14 (.X0(x0[13]), .X1(x1[13]), .X2(x2[13]), .X3(x3[13]), .s1(s1), .s0(s0), .Z(z[13]));
  MUX_4_1 mux_4_1_15 (.X0(x0[14]), .X1(x1[14]), .X2(x2[14]), .X3(x3[14]), .s1(s1), .s0(s0), .Z(z[14]));
  MUX_4_1 mux_4_1_16 (.X0(x0[15]), .X1(x1[15]), .X2(x2[15]), .X3(x3[15]), .s1(s1), .s0(s0), .Z(z[15]));
endmodule

module ALU (
  input  [15:0] A,
  input  [15:0] B,
  input  in_3,
  input  in_4,
  output [15:0] out_5,
  output N,
  output Z,
  output V,
  output C
);

  wire and_1_out, and_2_out, b15_prime, Cout0, Cout1, not_2_out, not_3_out, not_4_out, not_5_out;
  wire [15:0] adder_1_out, adder_2_out, not_1_out, xor_1_out;

  assign not_1_out = ~B;  // NOT_Gate not_1, 16 bits wide
  Adder #(.width(16)) adder_1 (.a(A), .b(not_1_out), .out(adder_1_out), .cin(1'b1), .cout(Cout1));
  or or_1 (C, Cout0, Cout1);
  Adder #(.width(16)) adder_2 (.a(A), .b(B), .out(adder_2_out), .cin(1'b0), .cout(Cout0));
  assign xor_1_out = A ^ B;  // XOR_Gate xor_1, 16 bits wide
  MUX_4_1 mux_4_1_1 (.X0(A[15]), .X3(not_2_out), .s1(in_3), .s0(in_3), .Z(b15_prime));  // open: X1, X2
  not not_2 (not_2_out, A[15]);
  MUX_4_1x16 mux_4_1x16_1 (
    .x0(adder_2_out), .x1(xor_1_out), .x2(B), .x3(adder_1_out), .s1(in_3), .s0(in_4), .z({N, out_5[14:0]}));
  not not_3 (not_3_out, B[15]);
  not not_4 (not_4_out, b15_prime);
  not not_5 (not_5_out, N);
  nor nor_1 (Z, out_5[0], out_5[1], out_5[2], out_5[3], out_5[4], out_5[5], out_5[6], out_5[7], out_5[8], out_5[9], out_5[10], out_5[11], out_5[12], out_5[13], out_5[14], N);
  and and_1 (and_1_out, not_3_out, not_4_out, N);
  and and_2 (and_2_out, B[15], b15_prime, not_5_out);
  or or_2 (V, and_1_out, and_2_out);

  assign out_5[15] = N;

  // Other names for the same wires on the sheet: b15 = A[15]; a15 = B[15]; s15 = N; T0 = in_4; T1 = in_3
endmodule
